# Fritzing sketch test_setup (saved by Fritzing 0.9.3b)
breadboards: 1

parts:
  Raspberry_Pi_1 = Raspberry Pi 3 [part_number=RPI-3-V1.2]
  LCD1 = LCD screen
  R4 = Resistor [tolerance=±5% resistance=10k package=THT]
  R5 = Resistor [tolerance=±5% resistance=10k package=THT]
  R6 = Resistor [tolerance=±5% resistance=10k package=THT]
  R7 = Resistor [tolerance=±5% resistance=10k package=THT]
  1k_Ohm_Contrast = TRIMPOT [package=trimpot_pth_s3_lock]
  R3 = Resistor [tolerance=±5% resistance=10k package=THT]
  R2 = Resistor [tolerance=±5% resistance=10k package=THT]
  R1 = Resistor [tolerance=±5% resistance=10k package=THT]

nets:
  N1: Raspberry_Pi_1.GPIO5, LCD1.DB4, R7.Pin_1
  N2: Raspberry_Pi_1.GPIO6, LCD1.DB5, R6.Pin_1
  N3: Raspberry_Pi_1.GPIO13, LCD1.DB6, R5.Pin_1
  N4: Raspberry_Pi_1.GPIO26, LCD1.DB7, R4.Pin_1
  GND: Raspberry_Pi_1.GND, LCD1.VSS, 1k_Ohm_Contrast.CW
  N5: Raspberry_Pi_1.GPIO21, LCD1.E, R1.Pin_1
  N6: Raspberry_Pi_1.GPIO20, LCD1.R/W, R2.Pin_1
  N7: Raspberry_Pi_1.GPIO16, LCD1.RS, R3.Pin_1
  5V: Raspberry_Pi_1.5V, LCD1.VDD, R4.Pin_0, R5.Pin_0, R6.Pin_0, R7.Pin_0, 1k_Ohm_Contrast.CCW, R3.Pin_0, R2.Pin_0, R1.Pin_0
  N8: LCD1.V0, 1k_Ohm_Contrast.WIPER
